# Fritzing sketch moisture_battery (saved by Fritzing 0.9.3b)
circuit board: 8.46667cm x 5.64444cm
breadboards: 1

parts:
  J2_DBG = female pin header, 2 pins [form="♀ (female)"]
  J1_SETUP = rounded female pin header, 2 pins [form="♀ (female rounded)"]
  R1 = Resistor [tolerance=±5% resistance=220 package=THT]
  Bauteil1 = SparkFun ESP8266 Thing
  R2 = Resistor [tolerance=±5% resistance=220 package=THT]
  VCC1 = Battery  # not connected
  J1 = JST-B3P-VH [part_number=JST-B3P-VH package=THT]
  Bauteil2 = Soil Moisture Sensor

nets:
  N1: J2_DBG.pin1, Bauteil1.GPIO16
  N2: J2_DBG.pin2, Bauteil1.RESET
  N3: J1_SETUP.pin1, Bauteil1.GPIO5
  GND: J1_SETUP.pin2, Bauteil1.GND, R2.Pin_1, J1.pin3, Bauteil2.GND
  N4: R1.Pin_0, Bauteil1.ADC, R2.Pin_0
  N5: R1.Pin_1, J1.pin1, Bauteil2.SIG
  N6: Bauteil1.GPIO4, J1.pin2, Bauteil2.VCC
